// Digital circuit hw3_a.dig as structural Verilog
module hw3_a (
  input  [3:0] X,
  input  [3:0] Y,
  output [3:0] Z
);

  wire comparator_1_eq;

  Comparator comparator_1 (.a(X[0]), .b(1'b0), .eq(comparator_1_eq));  // open: gt, lt
  Multiplexer multiplexer_1 (.sel(comparator_1_eq), .in_0(Y[0]), .in_1(X[0]), .out(Z[0]));
  // Pins of 1 and 4 bits meet at X
  // Pins of 1 and 4 bits meet at 4'b0000
  // Pins of 1 and 4 bits meet at Y
  // Pins of 1 and 4 bits meet at Z
endmodule
