// Digital circuit hw3_b.dig as structural Verilog
module hw3_b (
  input  [3:0] X,
  input  [3:0] Y,
  output [3:0] Z
);

  wire add_1_s, comparator_1_eq;

  Comparator comparator_1 (.a(X[0]), .b(Y[0]), .eq(comparator_1_eq));  // open: gt, lt
  Add add_1 (.a(X[0]), .b(Y[0]), .s(add_1_s));  // open: c_i, c_o
  Multiplexer multiplexer_1 (.sel(comparator_1_eq), .in_0(add_1_s), .in_1(Y[0]), .out(Z[0]));
  // Pins of 1 and 4 bits meet at X
  // Pins of 1 and 4 bits meet at Y
  // Pins of 1 and 4 bits meet at Z
endmodule
