// Digital circuit hw3_d.dig as structural Verilog
module hw3_d (
  input  [3:0] X,
  input  [3:0] Y,
  output [3:0] Z
);

  wire comparator_1_gt, multiplexer_1_out;

  Multiplexer multiplexer_1 (.sel(comparator_1_gt), .in_0(1'b1), .in_1(1'b0), .out(multiplexer_1_out));
  Comparator comparator_1 (.a(X[0]), .b(Y[0]), .gt(comparator_1_gt));  // open: eq, lt
  Add add_1 (.a(X[0]), .b(1'b1), .c_i(multiplexer_1_out), .s(Z[0]));  // open: c_o
  // Pins of 1 and 4 bits meet at X
  // Pins of 1 and 4 bits meet at Y
  // Pins of 1 and 4 bits meet at Z
  // Pins of 1 and 4 bits meet at 4'b0101
endmodule
