// Digital circuit hw3_a.dig as structural Verilog
module hw3_a (
  input  [3:0] X,
  input  [3:0] Y,
  output [3:0] Z
);

  wire comparator_1_eq;

  Comparator #(.Bits(4)) comparator_1 (.a(X), .b(4'b0000), .eq(comparator_1_eq));  // open: gt, lt
  Multiplexer #(.Bits(4)) multiplexer_1 (.sel(comparator_1_eq), .in_0(Y), .in_1(X), .out(Z));
endmodule
