// Digital circuit hw3_c.dig as structural Verilog
module hw3_c (
  input  [3:0] X,
  input  [3:0] Y,
  output [3:0] Z
);

  wire comparator_1_lt;
  wire [3:0] multiplexer_1_out;

  Multiplexer #(.Bits(4)) multiplexer_1 (
    .sel(comparator_1_lt), .in_0(4'b0110), .in_1(4'b0100), .out(multiplexer_1_out));
  Comparator #(.Bits(4)) comparator_1 (.a(X), .b(Y), .lt(comparator_1_lt));  // open: gt, eq
  Add #(.Bits(4)) add_1 (.a(X), .b(multiplexer_1_out), .c_i(1'b0), .s(Z));  // open: c_o
endmodule
